// Logisim project minikit_logisim.circ as structural Verilog: 28 circuits, main circuit main
module main (
  input  A,
  input  F,
  input  B,
  input  in_4,
  input  in_5,
  input  in_6,
  input  in_7,
  input  in_8,
  input  in_9,
  input  in_10,
  input  in_11,
  input  in_12,
  input  in_13,
  input  in_14,
  input  in_15,
  input  in_16,
  input  in_17,
  input  in_18,
  input  in_19,
  input  in_20,
  input  in_21,
  input  in_22,
  input  in_23,
  input  in_24,
  input  in_25,
  input  in_26,
  input  in_27,
  input  in_28,
  input  in_29,
  input  in_30,
  input  a_2,
  input  A_3,
  input  b_2,
  input  B_3,
  input  Carry_in,
  input  c,
  input  d,
  input  carry_in_2,
  input  a_4,
  input  x1,
  input  b_4,
  input  x2,
  input  Carry_in_3,
  input  carry_in_4,
  input  carry_in_5,
  input  [3:0] x1_2,
  input  [1:0] x1_3,
  input  [3:0] x2_2,
  input  [1:0] x2_3,
  input  D0,
  input  A0,
  input  A1,
  input  D1,
  input  D2,
  input  D3,
  input  [1:0] A_5,
  input  s1,
  input  s0,
  input  A0_2,
  input  A0_3,
  input  A1_2,
  input  A1_3,
  input  en1___1,
  input  Enable,
  input  en2a____0,
  input  en2b___0,
  input  [1:0] A_6,
  input  [1:0] A_7,
  input  en1___1_2,
  input  Enable_2,
  input  en2a____0_2,
  input  en2b___0_2,
  input  EN1,
  input  in_74,
  input  in_75,
  input  in_76,
  input  in_77,
  input  in_78,
  input  in_79,
  input  in_80,
  input  in_81,
  input  in_82,
  input  in_83,
  input  EN2A,
  input  EN2B,
  input  X0,
  input  \Seleção ,
  input  X1_4,
  output cout,
  output s,
  output Q0,
  output Q0_2,
  output Q2,
  output Q1,
  output Q1_2,
  output Q3,
  output Q2_2,
  output Q3_2,
  output Q0_3,
  output Q0_4,
  output Q0_5,
  output Q0_6,
  output Q2_3,
  output Q2_4,
  output Q1_3,
  output Q1_4,
  output Q1_5,
  output Q1_6,
  output Q3_3,
  output Q2_5,
  output Q3_4,
  output Q2_6,
  output Q3_5,
  output Q3_6
);

  wire adder_1_cout, adder_2_cout, adder_2_out, adder_3_cout, AND_2_out, AND_3_out, AND_4_out, AND_5_out,
       AND_6_out, AND_7_out, AND_8_out, AND_9_out, AND_10_out, AND_11_out, AND_12_out, AND_13_out,
       AND_14_out, AND_15_out, AND_16_out, AND_17_out, AND_18_out, AND_19_out, AND_24_out, AND_25_out,
       AND_26_out, AND_27_out, AND_28_out, AND_29_out, AND_30_out, AND_31_out, AND_32_out, AND_33_out,
       AND_34_out, AND_35_out, AND_36_out, AND_37_out, and_38_out, and_39_out, and_40_out, and_41_out,
       and_42_out, and_43_out, AND_52_out, AND_53_out, AND_54_out, AND_55_out, AND_56_out, AND_57_out,
       AND_58_out, AND_59_out, AND_60_out, AND_61_out, AND_out, NAND_2_out, NAND_3_out, NAND_4_out,
       NAND_5_out, NAND_6_out, NAND_7_out, NAND_8_out, NAND_9_out, NAND_10_out, NAND_11_out, NAND_12_out,
       NAND_13_out, NAND_14_out, NAND_15_out, NAND_out, NOR_out, not_1_out, not_2_out, not_3_out, not_4_out,
       not_5_out, not_6_out, not_7_out, not_8_out, not_9_out, not_10_out, not_11_out, not_12_out, not_13_out,
       not_14_out, not_15_out, not_16_out, not_17_out, not_18_out, not_19_out, not_20_out, not_21_out,
       not_22_out, not_23_out, not_24_out, not_25_out, not_26_out, not_27_out, not_28_out, not_29_out,
       not_30_out, not_31_out, not_32_out, not_33_out, not_34_out, not_35_out, not_36_out, not_37_out,
       not_38_out, not_39_out, not_40_out, not_41_out, not_42_out, not_43_out, not_44_out, not_45_out,
       not_46_out, OR_2_out, OR_3_out, or_4_out, OR_5_out, OR_6_out, OR_7_out, OR_8_out, OR_out, XOR_2_out,
       XOR_3_out, XOR_4_out, XOR_5_out, XOR_out;
  wire [1:0] adder_3_out;
  wire [3:0] adder_1_out;

  LED led_1 (.in(1'b0));
  LED led_2 (.in(1'b1));
  not not_1 (not_1_out, in_5);
  not not_2 (not_2_out, in_6);
  not not_3 (not_3_out, in_9);
  not not_4 (not_4_out, in_10);
  not not_5 (not_5_out, in_15);
  not not_6 (not_6_out, in_16);
  not not_7 (not_7_out, in_21);
  not not_8 (not_8_out, in_22);
  not not_9 (not_9_out, in_28);
  not not_10 (not_10_out, in_27);
  not not_11 (not_11_out, s1);
  not not_12 (not_12_out, in_74);
  not not_13 (not_13_out, in_75);
  and AND (AND_out, A, B);
  or OR (OR_out, not_1_out, not_2_out);
  nand NAND (NAND_out, in_7, in_8);
  or OR_2 (OR_2_out, not_3_out, not_4_out);
  or OR_3 (OR_3_out, in_11, in_13);
  and AND_2 (AND_2_out, not_5_out, not_6_out);
  nor NOR (NOR_out, in_17, in_19);
  and AND_3 (AND_3_out, not_7_out, not_8_out);
  xor XOR (XOR_out, in_23, in_25);
  and AND_4 (AND_4_out, in_27, not_9_out);
  or or_4 (or_4_out, AND_4_out, AND_5_out);
  and AND_5 (AND_5_out, not_10_out, in_28);
  not not_14 (not_14_out, in_29);
  nand NAND_2 (NAND_2_out, in_30, in_30);
  not not_15 (not_15_out, A0_3);
  not not_16 (not_16_out, A1_3);
  not not_17 (not_17_out, in_76);
  not not_18 (not_18_out, \Seleção );
  LED led_3 (.in(AND_out));
  not not_19 (not_19_out, OR_out);
  LED led_4 (.in(not_19_out));
  LED led_5 (.in(NAND_out));
  LED led_6 (.in(OR_2_out));
  LED led_7 (.in(OR_3_out));
  not not_20 (not_20_out, AND_2_out);
  LED led_8 (.in(not_20_out));
  LED led_9 (.in(NOR_out));
  LED led_10 (.in(AND_3_out));
  LED led_11 (.in(XOR_out));
  LED led_12 (.in(or_4_out));
  LED led_13 (.in(not_14_out));
  LED led_14 (.in(NAND_2_out));
  xor XOR_2 (XOR_2_out, A_3, B_3);
  xor XOR_3 (XOR_3_out, a_4, b_4);
  and AND_6 (AND_6_out, D0, not_11_out, not_21_out);
  not not_21 (not_21_out, s0);
  and AND_7 (AND_7_out, D1, not_11_out, s0);
  and AND_8 (AND_8_out, D2, s1, not_22_out);
  not not_22 (not_22_out, s0);
  and AND_9 (AND_9_out, D3, s1, s0);
  and AND_10 (AND_10_out, not_12_out, not_13_out, not_17_out);
  and AND_11 (AND_11_out, not_12_out, not_13_out, in_76);
  and AND_12 (AND_12_out, not_12_out, in_75, not_17_out);
  and AND_13 (AND_13_out, not_12_out, in_75, in_76);
  and AND_14 (AND_14_out, in_74, not_13_out, not_17_out);
  and AND_15 (AND_15_out, in_74, not_13_out, in_76);
  and AND_16 (AND_16_out, in_74, in_75, not_17_out);
  and AND_17 (AND_17_out, in_74, in_75, in_76);
  and AND_18 (AND_18_out, X0, not_18_out);
  and AND_19 (AND_19_out, X1_4, \Seleção );
  nand NAND_3 (NAND_3_out, F, in_4);
  nand NAND_4 (NAND_4_out, in_18, in_18);
  nand NAND_5 (NAND_5_out, in_20, in_20);
  nand NAND_6 (NAND_6_out, in_24, in_26);
  and AND_20 (Q0_6, not_15_out, Enable_2, not_16_out);
  and AND_21 (Q1_4, A0_3, Enable_2, not_16_out);
  and AND_22 (Q2_6, A1_3, Enable_2, not_15_out);
  and AND_23 (Q3_6, A1_3, Enable_2, A0_3);
  LED F0 (.in(AND_10_out));
  LED F1 (.in(AND_11_out));
  LED F2 (.in(AND_12_out));
  LED F3 (.in(AND_13_out));
  LED F4 (.in(AND_14_out));
  LED F5 (.in(AND_15_out));
  LED F6 (.in(AND_16_out));
  LED F7 (.in(AND_17_out));
  or OR_5 (OR_5_out, AND_18_out, AND_19_out);
  LED led_15 (.in(NAND_7_out));
  nand NAND_7 (NAND_7_out, NAND_3_out, NAND_3_out);
  nand NAND_8 (NAND_8_out, in_12, in_12);
  nand NAND_9 (NAND_9_out, NAND_8_out, NAND_10_out);
  nand NAND_10 (NAND_10_out, in_14, in_14);
  nand NAND_11 (NAND_11_out, NAND_4_out, NAND_5_out);
  nand NAND_12 (NAND_12_out, in_24, NAND_6_out);
  nand NAND_13 (NAND_13_out, NAND_6_out, in_26);
  xor XOR_4 (XOR_4_out, XOR_2_out, Carry_in);
  and AND_24 (AND_24_out, XOR_2_out, Carry_in);
  and AND_25 (AND_25_out, A_3, B_3);
  xor XOR_5 (XOR_5_out, XOR_3_out, Carry_in_3);
  and AND_26 (AND_26_out, b_4, a_4);
  and AND_27 (AND_27_out, b_4, Carry_in_3);
  and AND_28 (AND_28_out, a_4, Carry_in_3);
  LED led_16 (.in(OR_6_out));
  or OR_6 (OR_6_out, AND_6_out, AND_7_out, AND_8_out, AND_9_out);
  Decoder #(.select(2)) decoder_1 (.out0(Q0_3), .out1(Q2_3), .out2(Q1_5), .out3(Q3_3), .sel(A_6), .en(Enable));
  not not_23 (not_23_out, in_77);
  LED saida (.in(OR_5_out));
  LED led_17 (.in(NAND_9_out));
  nand NAND_14 (NAND_14_out, NAND_11_out, NAND_11_out);
  LED led_18 (.in(NAND_14_out));
  LED led_19 (.in(NAND_15_out));
  nand NAND_15 (NAND_15_out, NAND_12_out, NAND_13_out);
  LED \Saída  (.in(XOR_4_out));
  or OR_7 (OR_7_out, AND_24_out, AND_25_out);
  LED Carry_out (.in(OR_7_out));
  LED led_20 (.in(XOR_5_out));
  LED led_21 (.in(OR_8_out));
  or OR_8 (OR_8_out, AND_26_out, AND_27_out, AND_28_out);
  not not_24 (not_24_out, in_79);
  not not_25 (not_25_out, in_78);
  not not_26 (not_26_out, A0);
  not not_27 (not_27_out, A1);
  not not_28 (not_28_out, en2a____0_2);
  not not_29 (not_29_out, en2b___0_2);
  and AND_29 (AND_29_out, not_23_out, not_25_out, in_80, not_24_out);
  and AND_30 (AND_30_out, not_23_out, not_25_out, in_80, in_79);
  and AND_31 (AND_31_out, not_23_out, in_78, in_80, not_24_out);
  and AND_32 (AND_32_out, not_23_out, in_78, in_80, in_79);
  and AND_33 (AND_33_out, in_77, not_25_out, in_80, not_24_out);
  and AND_34 (AND_34_out, in_77, not_25_out, in_80, in_79);
  and AND_35 (AND_35_out, in_77, in_78, in_80, not_24_out);
  and AND_36 (AND_36_out, in_77, in_78, in_80, in_79);
  not not_30 (not_30_out, A0_2);
  not not_31 (not_31_out, A1_2);
  and AND_37 (AND_37_out, en1___1_2, not_28_out, not_29_out);
  LED F0_2 (.in(AND_29_out));
  LED F1_2 (.in(AND_30_out));
  LED F2_2 (.in(AND_31_out));
  LED F3_2 (.in(AND_32_out));
  LED F4_2 (.in(AND_33_out));
  LED F5_2 (.in(AND_34_out));
  LED F6_2 (.in(AND_35_out));
  LED F7_2 (.in(AND_36_out));
  and and_38 (and_38_out, a_2, b_2);
  and and_39 (and_39_out, a_2, c);
  and and_40 (and_40_out, b_2, c);
  and and_41 (and_41_out, a_2, d);
  and and_42 (and_42_out, b_2, d);
  and and_43 (and_43_out, c, d);
  xor odd_parity_1 (s, a_2, b_2, c, d);
  and AND_44 (Q0_2, not_26_out, not_27_out);
  and AND_45 (Q1, A0, not_27_out);
  and AND_46 (Q2_2, A1, not_26_out);
  and AND_47 (Q3_2, A1, A0);
  or or_9 (cout, and_38_out, and_39_out, and_40_out, and_41_out, and_42_out, and_43_out);
  // Probe on adder_1_out
  Adder #(.width(4)) adder_1 (.a(x1_2), .b(x2_2), .out(adder_1_out), .cin(carry_in_4), .cout(adder_1_cout));
  // Probe on adder_1_cout
  and AND_48 (Q0_4, not_30_out, AND_37_out, not_31_out);
  and AND_49 (Q1_3, A0_2, AND_37_out, not_31_out);
  and AND_50 (Q2_5, A1_2, AND_37_out, not_30_out);
  and AND_51 (Q3_5, A1_2, AND_37_out, A0_2);
  not not_32 (not_32_out, in_81);
  not not_33 (not_33_out, in_82);
  Decoder #(.select(2), .enable("false")) decoder_2 (.out0(Q0), .out1(Q2), .out2(Q1_2), .out3(Q3), .sel(A_5));
  not not_34 (not_34_out, in_83);
  not not_35 (not_35_out, en2a____0);
  not not_36 (not_36_out, en2b___0);
  and AND_52 (AND_52_out, EN1, not_45_out, not_46_out);
  Adder #(.width(1)) adder_2 (.a(x1), .b(x2), .out(adder_2_out), .cin(carry_in_2), .cout(adder_2_cout));
  // Probe on adder_2_out
  // Probe on adder_2_cout
  Adder #(.width(2)) adder_3 (.a(x1_3), .b(x2_3), .out(adder_3_out), .cin(carry_in_5), .cout(adder_3_cout));
  // Probe on adder_3_out
  // Probe on adder_3_cout
  and AND_53 (AND_53_out, en1___1, not_35_out, not_36_out);
  not not_37 (not_37_out, AND_54_out);
  and AND_54 (AND_54_out, not_32_out, not_33_out, AND_52_out, not_34_out);
  not not_38 (not_38_out, AND_55_out);
  and AND_55 (AND_55_out, not_32_out, not_33_out, AND_52_out, in_83);
  and AND_56 (AND_56_out, not_32_out, in_82, AND_52_out, not_34_out);
  not not_39 (not_39_out, AND_56_out);
  and AND_57 (AND_57_out, not_32_out, in_82, AND_52_out, in_83);
  not not_40 (not_40_out, AND_57_out);
  and AND_58 (AND_58_out, in_81, not_33_out, AND_52_out, not_34_out);
  not not_41 (not_41_out, AND_58_out);
  not not_42 (not_42_out, AND_59_out);
  and AND_59 (AND_59_out, in_81, not_33_out, AND_52_out, in_83);
  not not_43 (not_43_out, AND_60_out);
  and AND_60 (AND_60_out, in_81, in_82, AND_52_out, not_34_out);
  and AND_61 (AND_61_out, in_81, in_82, AND_52_out, in_83);
  not not_44 (not_44_out, AND_61_out);
  not not_45 (not_45_out, EN2A);
  not not_46 (not_46_out, EN2B);
  Decoder #(.select(2)) decoder_3 (.out0(Q0_5), .out1(Q2_4), .out2(Q1_6), .out3(Q3_4), .sel(A_7), .en(AND_53_out));
  LED F0_3 (.in(not_37_out));
  LED F1_3 (.in(not_38_out));
  LED F2_3 (.in(not_39_out));
  LED F3_3 (.in(not_40_out));
  LED F4_3 (.in(not_41_out));
  LED F5_3 (.in(not_42_out));
  LED F6_3 (.in(not_43_out));
  LED F7_3 (.in(not_44_out));

  // Notes on the sheet:
  //   Porta Conectivo de Sheffer (NAND)
  //   Não (NOT)
  //   X
  //   Y
  //   Porta E (AND)
  //   Porta OU (OR)
  //   Porta  (NOR)
  //   Porta XOU (XOR)
  //   NOT
  //   Somador Completo de 1 bits
  //   Multiplexador de 4 entradas
  //   Decodificador de 3 entradas e 8 saidas
  //   Z
  //   Multiplexador 2 para 1
  //   A.B=F
  //   A+B=F
  //   A=F
  //   Decodificador de 2 entradas e 4 saídas com enable
  //   A+B=F
  //   A⊕B=F
  //   X
  //   input
  //   A
  //   0
  //   0
  //   1
  //   1
  //   A
  //   0
  //   0
  //   1
  //   1
  //   input
  //   A
  //   0
  //   0
  //   1
  //   1
  //   Y
  //   Z
  //   Y
  //   B
  //   0
  //   1
  //   0
  //   1
  //   A.B=F
  //   input
  //   B
  //   0
  //   1
  //   0
  //   1
  //   B
  //   0
  //   1
  //   0
  //   1
  //   input
  //   A
  //   B
  //   0
  //   0
  //   1
  //   0
  //   0
  //   1
  //   1
  //   1
  //   input
  //   A
  //   B
  //   0
  //   0
  //   1
  //   0
  //   0
  //   1
  //   1
  //   1
  //   s
  //   carry out
  //   Decodificador de 3 entradas e 8 saidas com enable
  //   output
  //   F
  //   0
  //   0
  //   0
  //   1
  //   output
  //   F
  //   1
  //   1
  //   1
  //   0
  //   output
  //   F
  //   0
  //   1
  //   1
  //   1
  //   output
  //   F
  //   1
  //   0
  //   0
  //   0
  //   output
  //   F
  //   0
  //   1
  //   1
  //   0
  //   Enable
  //   Decodificador de 2 entradas e 4 saídas
  //   Somador  de 4 bits
  //   Somador de 4  bits
  //   Decodificador de 2 entradas e 4 saídas com enable de 3
  //   X
  //   Y
  //   Chip 74x138
  //   Z
  //   Somador de 1 bit
  //   Somador de 2  bits
  //   Enable
endmodule

module circuitos (
  input  a,
  input  x,
  input  b,
  input  y,
  input  c,
  input  z,
  input  d,
  input  x_2,
  input  y_2,
  input  z_2,
  input  in_11,
  input  in_12,
  input  in_13,
  input  in_14,
  output cout,
  output s
);

  wire and_1_out, and_2_out, and_3_out, and_4_out, and_5_out, and_6_out, and_7_out, and_8_out, and_9_out,
       and_10_out, and_11_out, and_12_out, and_13_out, nand_1_out, nor_1_out, not_1_out, not_2_out,
       not_3_out, not_4_out, not_5_out, not_6_out, not_7_out, not_8_out, not_9_out, not_10_out, not_11_out,
       or_2_out, or_3_out, or_4_out, xnor_1_out, xnor_2_out, xor_1_out, xor_2_out;

  and and_1 (and_1_out, a, b);
  and and_2 (and_2_out, a, c);
  and and_3 (and_3_out, b, c);
  and and_4 (and_4_out, a, d);
  and and_5 (and_5_out, b, d);
  and and_6 (and_6_out, c, d);
  xor odd_parity_1 (s, a, b, c, d);
  or or_1 (cout, and_1_out, and_2_out, and_3_out, and_4_out, and_5_out, and_6_out);
  not not_1 (not_1_out, x);
  not not_2 (not_2_out, y);
  not not_3 (not_3_out, z);
  not not_4 (not_4_out, x);
  not not_5 (not_5_out, y);
  not not_6 (not_6_out, x_2);
  and and_7 (and_7_out, not_6_out, y_2);
  not not_7 (not_7_out, y_2);
  not not_8 (not_8_out, in_14);
  and and_8 (and_8_out, not_1_out, not_2_out, not_3_out);
  and and_9 (and_9_out, not_4_out, z, not_5_out);
  not not_9 (not_9_out, and_7_out);
  not not_10 (not_10_out, or_2_out);
  or or_2 (or_2_out, x_2, not_7_out, z_2);
  nor nor_1 (nor_1_out, in_11, in_13, in_14);
  and and_10 (and_10_out, in_11, in_12);
  not not_11 (not_11_out, in_13);
  xor xor_1 (xor_1_out, in_13, in_14);
  xnor xnor_1 (xnor_1_out, in_11, in_12);
  and and_11 (and_11_out, in_13, not_8_out);
  or or_3 (or_3_out, and_8_out, and_9_out);
  xnor xnor_2 (xnor_2_out, not_9_out, not_10_out);
  or or_4 (or_4_out, not_11_out, xor_1_out);
  and and_12 (and_12_out, xnor_1_out, and_11_out);
  LED led_1 (.in(or_3_out));
  and and_13 (and_13_out, and_10_out, or_4_out);
  nand nand_1 (nand_1_out, xnor_2_out, z_2);
  LED led_2 (.in(nand_1_out));
  ExactlyOne xor_2 (.out(xor_2_out), .in0(nor_1_out), .in1(and_13_out), .in2(and_12_out));
  LED led_3 (.in(xor_2_out));

  // Notes on the sheet:
  //   f3
  //   W
endmodule

module lista_7 (
  input  A0,
  input  A1,
  input  en1___1,
  input  en2a____0,
  input  en2b___0,
  input  [1:0] A,
  input  en1___1_2,
  input  en2a____0_2,
  input  en2b___0_2,
  input  A0_2,
  input  A1_2,
  input  en1___1_3,
  input  en2a____0_3,
  input  en2b___0_3,
  output Q0,
  output Q0_2,
  output Q2,
  output Q1,
  output Q1_2,
  output Q2_2,
  output Q3,
  output Q3_2,
  output Q0_3,
  output Q1_3,
  output Q2_3,
  output Q3_3
);

  wire AND_2_out, AND_7_out, AND_8_out, AND_9_out, AND_10_out, AND_11_out, AND_out, not_1_out, not_2_out,
       not_3_out, not_4_out, not_5_out, not_6_out, not_7_out, not_8_out, not_13_out, not_14_out;

  not not_1 (not_1_out, en2a____0_2);
  not not_2 (not_2_out, en2b___0_2);
  not not_3 (not_3_out, A0);
  not not_4 (not_4_out, A1);
  and AND (AND_out, en1___1_2, not_1_out, not_2_out);
  not not_5 (not_5_out, A0_2);
  not not_6 (not_6_out, A1_2);
  and AND_2 (AND_2_out, en1___1_3, not_7_out, not_8_out);
  not not_7 (not_7_out, en2a____0_3);
  not not_8 (not_8_out, en2b___0_3);
  and AND_3 (Q0, not_3_out, AND_out, not_4_out);
  and AND_4 (Q1, A0, AND_out, not_4_out);
  and AND_5 (Q2_2, A1, AND_out, not_3_out);
  and AND_6 (Q3_2, A1, AND_out, A0);
  and AND_7 (AND_7_out, not_5_out, AND_2_out, not_6_out);
  and AND_8 (AND_8_out, A0_2, AND_2_out, not_6_out);
  and AND_9 (AND_9_out, A1_2, AND_2_out, not_5_out);
  and AND_10 (AND_10_out, A1_2, AND_2_out, A0_2);
  not not_9 (Q0_3, AND_7_out);
  not not_10 (Q1_3, AND_8_out);
  not not_11 (Q2_3, AND_9_out);
  not not_12 (Q3_3, AND_10_out);
  not not_13 (not_13_out, en2a____0);
  not not_14 (not_14_out, en2b___0);
  Decoder #(.select(2)) decoder_1 (.out0(Q0_2), .out1(Q2), .out2(Q1_2), .out3(Q3), .sel(A), .en(AND_11_out));
  and AND_11 (AND_11_out, en1___1, not_13_out, not_14_out);

  // Notes on the sheet:
  //   1)
  //   C)
  //   Enable
  //   Enable
  //   Decodificador de 2 entradas e 4 saídas com enable de 3
  //   D) Saidas do decodificador ativas em nível baixo
  //   Enable
endmodule

module Prova_2 (
  input  A0,
  input  A1,
  input  Enable,
  input  [1:0] A,
  input  Enable_2,
  input  [3:0] A_B_C_D,
  output Q0,
  output Q0_2,
  output Q3,
  output Q2,
  output Q1,
  output Q1_2,
  output Q3_2,
  output Q2_2,
  output Q3_3
);

  wire decoder_1_out0, decoder_1_out1, decoder_1_out2, decoder_1_out3, decoder_1_out4, decoder_1_out5,
       decoder_1_out6, decoder_1_out7, decoder_1_out8, decoder_1_out9, decoder_1_out10, decoder_1_out11,
       decoder_1_out12, decoder_1_out13, decoder_1_out14, decoder_1_out15, not_1_out, not_2_out, not_3_out,
       not_4_out;

  not not_1 (not_1_out, A0);
  not not_2 (not_2_out, A1);
  Decoder #(.select(4), .enable("false")) decoder_1 (
    .out0(decoder_1_out0), .out1(decoder_1_out1), .out2(decoder_1_out2), .out3(decoder_1_out3),
    .out4(decoder_1_out4), .out5(decoder_1_out5), .out6(decoder_1_out6), .out7(decoder_1_out7),
    .out8(decoder_1_out8), .out9(decoder_1_out9), .out10(decoder_1_out10), .out11(decoder_1_out11),
    .out12(decoder_1_out12), .out13(decoder_1_out13), .out14(decoder_1_out14), .out15(decoder_1_out15),
    .sel(A_B_C_D));
  and AND (Q0_2, not_1_out, Enable_2, not_2_out);
  and AND_2 (Q1, A0, Enable_2, not_2_out);
  and AND_3 (Q2_2, A1, Enable_2, not_1_out);
  and AND_4 (Q3_3, A1, Enable_2, A0);
  // Probe on decoder_1_out0
  // Probe on decoder_1_out1
  Decoder #(.select(2)) decoder_2 (.out0(Q0), .out1(Q2), .out2(Q1_2), .out3(Q3_2), .sel(A), .en(Enable));
  // Probe on decoder_1_out2
  // NOT_Gate not_3 has open pins: in=open, out=not_3_out
  // NOT_Gate not_4 has open pins: in=open, out=not_4_out
  and AND_5 (Q3, not_3_out, not_4_out);

  // Notes on the sheet:
  //   Decodificador de 2 entradas e 4 saídas com enable
endmodule

module questao_2_prova_2_a (
  input  a,
  input  b,
  input  c,
  input  d,
  output y
);

  wire and_1_out, and_2_out, and_3_out, and_4_out, not_1_out, not_2_out, not_3_out, not_4_out, not_5_out,
       not_6_out;

  not not_1 (not_1_out, a);
  and and_1 (and_1_out, not_1_out, b, not_2_out);
  not not_2 (not_2_out, c);
  and and_2 (and_2_out, a, not_3_out, d);
  not not_3 (not_3_out, b);
  and and_3 (and_3_out, a, not_4_out, not_5_out);
  not not_4 (not_4_out, c);
  not not_5 (not_5_out, d);
  and and_4 (and_4_out, b, not_6_out, d);
  not not_6 (not_6_out, c);
  or or_1 (y, and_1_out, and_2_out, and_3_out, and_4_out);
endmodule

module questao_2_prova_2_b (
  input  a,
  input  b,
  input  c,
  input  d,
  output y
);

  wire and_1_out, and_2_out, and_3_out, and_4_out, not_1_out, not_2_out, not_3_out, not_4_out, not_5_out,
       not_6_out;

  not not_1 (not_1_out, a);
  and and_1 (and_1_out, not_1_out, b, not_2_out);
  not not_2 (not_2_out, c);
  not not_3 (not_3_out, a);
  and and_2 (and_2_out, not_3_out, b, d);
  not not_4 (not_4_out, a);
  and and_3 (and_3_out, not_4_out, not_5_out, d);
  not not_5 (not_5_out, c);
  not not_6 (not_6_out, c);
  and and_4 (and_4_out, b, not_6_out, d);
  or or_1 (y, and_1_out, and_2_out, and_3_out, and_4_out);
endmodule

module questao_2_prova_2_c (
  input  a,
  input  b,
  input  c,
  input  d,
  output y
);

  wire and_1_out, and_2_out, and_3_out, and_4_out;

  and and_1 (and_1_out, a, b, c);
  and and_2 (and_2_out, a, b, d);
  and and_3 (and_3_out, a, c, d);
  and and_4 (and_4_out, b, c, d);
  or or_1 (y, and_1_out, and_2_out, and_3_out, and_4_out);
endmodule

module questao_2_prova_2_d (
  input  a,
  input  b,
  input  c,
  input  d,
  output y
);

  wire and_1_out, and_2_out, and_3_out, and_4_out, not_1_out, not_2_out, not_3_out, not_4_out, not_5_out;

  not not_1 (not_1_out, b);
  and and_1 (and_1_out, a, not_1_out, c);
  not not_2 (not_2_out, b);
  and and_2 (and_2_out, a, not_2_out, d);
  not not_3 (not_3_out, c);
  and and_3 (and_3_out, a, not_3_out, not_4_out);
  not not_4 (not_4_out, d);
  and and_4 (and_4_out, b, c, not_5_out);
  not not_5 (not_5_out, d);
  or or_1 (y, and_1_out, and_2_out, and_3_out, and_4_out);
endmodule

module questao_2_prova_2_e (
  input  a,
  input  b,
  input  c,
  input  d,
  output y
);

  wire and_1_out, and_2_out, and_3_out, and_4_out, not_1_out, not_2_out, not_3_out, not_4_out, not_5_out;

  and and_1 (and_1_out, a, not_1_out, c);
  not not_1 (not_1_out, b);
  not not_2 (not_2_out, a);
  and and_2 (and_2_out, not_2_out, b, d);
  not not_3 (not_3_out, a);
  not not_4 (not_4_out, c);
  and and_3 (and_3_out, not_3_out, not_4_out, d);
  and and_4 (and_4_out, b, c, not_5_out);
  not not_5 (not_5_out, d);
  or or_1 (y, and_1_out, and_2_out, and_3_out, and_4_out);
endmodule

module \Questão_3  (
  input  in_1,
  input  in_2,
  input  in_3,
  input  [2:0] _2_1_0
);

  wire and_1_out, decoder_1_out0, decoder_1_out1, decoder_1_out2, decoder_1_out3, decoder_1_out4,
       decoder_1_out5, decoder_1_out6, decoder_1_out7, not_1_out, not_2_out, not_3_out, not_4_out, not_5_out,
       not_6_out, not_7_out, not_8_out, not_9_out;

  not not_1 (not_1_out, in_1);
  and and_1 (and_1_out, not_1_out, in_2, in_3);
  Decoder #(.select(3)) decoder_1 (
    .out0(decoder_1_out0), .out1(decoder_1_out1), .out2(decoder_1_out2), .out3(decoder_1_out3),
    .out4(decoder_1_out4), .out5(decoder_1_out5), .out6(decoder_1_out6), .out7(decoder_1_out7), .sel(_2_1_0),
    .en(and_1_out));
  not not_2 (not_2_out, decoder_1_out0);
  not not_3 (not_3_out, decoder_1_out1);
  not not_4 (not_4_out, decoder_1_out2);
  not not_5 (not_5_out, decoder_1_out3);
  not not_6 (not_6_out, decoder_1_out4);
  not not_7 (not_7_out, decoder_1_out5);
  not not_8 (not_8_out, decoder_1_out6);
  not not_9 (not_9_out, decoder_1_out7);
endmodule

module \Questão_4  (
  input  in_1,
  input  in_2,
  input  in_3,
  input  in_4,
  input  in_5,
  input  in_6,
  input  in_7,
  input  in_8,
  input  in_9,
  input  Enable,
  input  in_11,
  input  [2:0] _2_1_0,
  input  in_13,
  input  [2:0] in_14,
  input  A,
  input  B,
  input  C,
  input  D
);

  wire and_1_out, decoder_1_out0, decoder_1_out1, decoder_1_out2, decoder_1_out3, decoder_1_out4,
       decoder_1_out5, decoder_1_out6, decoder_1_out7, multiplexer_1_out, multiplexer_2_out,
       multiplexer_3_out, not_1_out, not_2_out, not_3_out, not_4_out, not_5_out, not_6_out, not_7_out,
       not_8_out, not_9_out, not_10_out, not_11_out, or_1_out;

  not not_1 (not_1_out, in_5);
  not not_2 (not_2_out, D);
  Decoder #(.select(3)) decoder_1 (
    .out0(decoder_1_out0), .out1(decoder_1_out1), .out2(decoder_1_out2), .out3(decoder_1_out3),
    .out4(decoder_1_out4), .out5(decoder_1_out5), .out6(decoder_1_out6), .out7(decoder_1_out7), .sel(_2_1_0),
    .en(and_1_out));
  and and_1 (and_1_out, not_1_out, in_7, in_9);
  not not_3 (not_3_out, decoder_1_out0);
  not not_4 (not_4_out, decoder_1_out1);
  not not_5 (not_5_out, decoder_1_out2);
  not not_6 (not_6_out, decoder_1_out3);
  not not_7 (not_7_out, decoder_1_out4);
  not not_8 (not_8_out, decoder_1_out5);
  not not_9 (not_9_out, decoder_1_out6);
  not not_10 (not_10_out, decoder_1_out7);
  Multiplexer #(.select(2), .disabled(0)) multiplexer_1 (
    .in0(1'b0), .in1(1'b0), .in2(1'b1), .in3(1'b1), .out(multiplexer_1_out), .sel({B, C}), .en(not_11_out));
  not not_11 (not_11_out, A);
  Multiplexer #(.select(2), .disabled(0)) multiplexer_2 (
    .in0(1'b0), .in1(D), .in2(not_2_out), .in3(1'b0), .out(multiplexer_2_out), .sel({B, C}), .en(A));
  or or_1 (or_1_out, multiplexer_1_out, multiplexer_2_out);
  // Probe on or_1_out
  // Probe on multiplexer_3_out
  Multiplexer #(.select(3)) multiplexer_3 (
    .in0(in_1), .in1(in_2), .in2(in_3), .in3(in_4), .in4(in_6), .in5(in_8), .in6(in_11), .in7(in_13),
    .out(multiplexer_3_out), .sel(in_14), .en(Enable));
endmodule

module \Questão_4_a  (
  input  a,
  input  b,
  input  c,
  input  d,
  output y
);

  wire and_1_out, and_2_out, and_3_out, not_1_out, not_2_out, not_3_out, not_4_out;

  not not_1 (not_1_out, a);
  not not_2 (not_2_out, b);
  not not_3 (not_3_out, c);
  not not_4 (not_4_out, d);
  and and_1 (and_1_out, not_1_out, b);
  and and_2 (and_2_out, a, not_2_out, c, d);
  or or_1 (y, and_1_out, and_2_out, and_3_out);
  and and_3 (and_3_out, a, b, not_3_out, not_4_out);
endmodule

module \Questão_4_B  (
  input  a,
  input  b,
  input  c,
  input  d,
  output y
);

  wire and_1_out, and_2_out, and_3_out, not_1_out, not_2_out, not_3_out, not_4_out, not_5_out;

  not not_1 (not_1_out, a);
  not not_2 (not_2_out, a);
  not not_3 (not_3_out, d);
  not not_4 (not_4_out, c);
  not not_5 (not_5_out, d);
  and and_1 (and_1_out, not_1_out, b);
  and and_2 (and_2_out, not_2_out, b, c, not_3_out);
  or or_1 (y, and_1_out, and_2_out, and_3_out);
  and and_3 (and_3_out, a, b, not_4_out, not_5_out);
endmodule

module \Questão_4_C  (
  input  a,
  input  b,
  input  c,
  input  d,
  output y
);

  wire and_1_out, and_2_out, and_3_out, not_1_out, not_2_out, not_3_out, not_4_out, not_5_out, not_6_out;

  not not_1 (not_1_out, a);
  not not_2 (not_2_out, a);
  not not_3 (not_3_out, d);
  not not_4 (not_4_out, a);
  not not_5 (not_5_out, b);
  not not_6 (not_6_out, c);
  and and_1 (and_1_out, not_1_out, b);
  and and_2 (and_2_out, not_2_out, b, c, not_3_out);
  or or_1 (y, and_1_out, and_2_out, and_3_out);
  and and_3 (and_3_out, not_4_out, not_5_out, not_6_out, d);
endmodule

module \uestão_4_D  (
  input  a,
  input  b,
  input  c,
  input  d,
  output y
);

  wire and_1_out, and_2_out, and_3_out, not_1_out, not_2_out, not_3_out, not_4_out, not_5_out;

  not not_1 (not_1_out, b);
  not not_2 (not_2_out, b);
  not not_3 (not_3_out, a);
  not not_4 (not_4_out, b);
  not not_5 (not_5_out, c);
  and and_1 (and_1_out, a, not_1_out);
  or or_1 (y, and_1_out, and_2_out, and_3_out);
  and and_2 (and_2_out, a, not_2_out, c, d);
  and and_3 (and_3_out, not_3_out, not_4_out, not_5_out, d);
endmodule

module \Questão_5  (
  input  a,
  input  b,
  input  c,
  input  d,
  input  e,
  input  f,
  output y
);

  wire decoder_1_out1, decoder_1_out5, decoder_1_out6, or_1_out;

  Decoder #(.select(3), .enable("false")) decoder_1 (
    .out1(decoder_1_out1), .out5(decoder_1_out5), .out6(decoder_1_out6), .sel({a, b, c}));  // open: out0, out2, out3, out4, out7
  or or_1 (or_1_out, decoder_1_out1, decoder_1_out5);
  Multiplexer #(.select(3), .enable("false")) multiplexer_1 (
    .in0(1'b0), .in1(1'b0), .in2(1'b0), .in3(1'b1), .in4(or_1_out), .in5(decoder_1_out6), .in6(1'b0),
    .in7(1'b0), .out(y), .sel({d, e, f}));
endmodule

module \Questão_5_A  (
  input  a,
  input  b,
  input  c,
  input  d,
  input  e,
  input  f,
  output y
);

  wire and_1_out, and_2_out, and_3_out, not_1_out, not_2_out, not_3_out, not_4_out, not_5_out, not_6_out,
       not_7_out;

  not not_1 (not_1_out, f);
  not not_2 (not_2_out, c);
  not not_3 (not_3_out, d);
  not not_4 (not_4_out, a);
  not not_5 (not_5_out, b);
  not not_6 (not_6_out, d);
  not not_7 (not_7_out, e);
  and and_1 (and_1_out, d, e, not_1_out);
  and and_2 (and_2_out, b, not_2_out, not_3_out, e, f);
  and and_3 (and_3_out, not_4_out, not_5_out, c, not_6_out, not_7_out, f);
  or or_1 (y, and_1_out, and_2_out, and_3_out);
endmodule

module \Questão_5_B  (
  input  a,
  input  b,
  input  c,
  input  d,
  input  e,
  input  f,
  output y
);

  wire and_1_out, and_2_out, and_3_out, not_1_out, not_2_out, not_3_out, not_4_out, not_5_out, not_6_out,
       not_7_out, not_8_out;

  not not_1 (not_1_out, f);
  not not_2 (not_2_out, b);
  not not_3 (not_3_out, e);
  not not_4 (not_4_out, f);
  not not_5 (not_5_out, a);
  not not_6 (not_6_out, b);
  not not_7 (not_7_out, d);
  not not_8 (not_8_out, e);
  and and_1 (and_1_out, d, e, not_1_out);
  and and_2 (and_2_out, not_2_out, c, d, not_3_out, not_4_out);
  and and_3 (and_3_out, not_5_out, not_6_out, c, not_7_out, not_8_out, f);
  or or_1 (y, and_1_out, and_2_out, and_3_out);
endmodule

module \Questão_5_C  (
  input  a,
  input  b,
  input  c,
  input  d,
  input  e,
  input  f,
  output y
);

  wire and_1_out, and_2_out, and_3_out, not_1_out, not_2_out, not_3_out, not_4_out, not_5_out, not_6_out;

  not not_1 (not_1_out, f);
  not not_2 (not_2_out, b);
  not not_3 (not_3_out, e);
  not not_4 (not_4_out, f);
  not not_5 (not_5_out, c);
  not not_6 (not_6_out, e);
  and and_1 (and_1_out, d, e, not_1_out);
  and and_2 (and_2_out, not_2_out, c, d, not_3_out, not_4_out);
  and and_3 (and_3_out, a, b, not_5_out, d, not_6_out, f);
  or or_1 (y, and_1_out, and_2_out, and_3_out);
endmodule

module \Questão_5_D  (
  input  a,
  input  b,
  input  c,
  input  d,
  input  e,
  input  f,
  output y
);

  wire and_1_out, and_2_out, and_3_out, not_1_out, not_2_out, not_3_out, not_4_out, not_5_out, not_6_out,
       not_7_out;

  not not_1 (not_1_out, d);
  not not_2 (not_2_out, c);
  not not_3 (not_3_out, d);
  not not_4 (not_4_out, a);
  not not_5 (not_5_out, b);
  not not_6 (not_6_out, d);
  not not_7 (not_7_out, e);
  and and_1 (and_1_out, not_1_out, e, f);
  and and_2 (and_2_out, b, not_2_out, not_3_out, e, f);
  and and_3 (and_3_out, not_4_out, not_5_out, c, not_6_out, not_7_out, f);
  or or_1 (y, and_1_out, and_2_out, and_3_out);
endmodule

module \Questão_5_E  (
  input  a,
  input  b,
  input  c,
  input  d,
  input  e,
  input  f,
  output y
);

  wire and_1_out, and_2_out, and_3_out, not_1_out, not_2_out, not_3_out, not_4_out, not_5_out, not_6_out;

  not not_1 (not_1_out, d);
  not not_2 (not_2_out, b);
  not not_3 (not_3_out, e);
  not not_4 (not_4_out, f);
  not not_5 (not_5_out, c);
  not not_6 (not_6_out, e);
  and and_1 (and_1_out, not_1_out, e, f);
  and and_2 (and_2_out, not_2_out, c, d, not_3_out, not_4_out);
  and and_3 (and_3_out, a, b, not_5_out, d, not_6_out, f);
  or or_1 (y, and_1_out, and_2_out, and_3_out);
endmodule

module \Questão_6  (
  input  i0,
  input  i0_2,
  input  [1:0] in_3,
  input  i0_3,
  input  i1,
  input  in_6,
  input  i2,
  input  in_8,
  input  i3,
  input  i0_4,
  input  Ei,
  input  i0_5,
  input  i0_6,
  input  [1:0] in_14,
  input  i0_7,
  input  Ra,
  input  Rb,
  input  Rc,
  input  Rd,
  input  Re,
  input  Rf,
  input  Rg,
  input  Rh,
  input  a,
  input  b,
  input  c,
  input  d,
  input  e,
  input  f,
  input  g,
  input  h
);

  wire buffer_1_out, buffer_9_out, decoder_1_out0, decoder_1_out1, decoder_1_out2, decoder_1_out3,
       decoder_2_out0, decoder_2_out1, decoder_2_out2, decoder_2_out3, decoder_2_out4, decoder_2_out5,
       decoder_2_out6, decoder_2_out7, not_1_out, or_3_out, priority_encoder_1_en_out, priority_encoder_1_gs,
       priority_encoder_2_en_out, priority_encoder_3_en_out, priority_encoder_3_gs, priority_encoder_4_p3,
       priority_encoder_4_p5, priority_encoder_4_p6, priority_encoder_4_p7, priority_encoder_4_p8;
  wire [1:0] priority_encoder_1_out, priority_encoder_2_out, priority_encoder_3_out;
  wire [2:0] or_2_out;

  // Probe on not_1_out
  not not_1 (not_1_out, priority_encoder_1_en_out);
  // Probe on priority_encoder_1_out
  Priority_Encoder #(.select(2)) priority_encoder_1 (
    .in0(i0_2), .in1(i1), .in2(i2), .in3(i3), .out(priority_encoder_1_out), .gs(priority_encoder_1_gs),
    .en_out(priority_encoder_1_en_out), .en_in(Ei));
  // Probe on priority_encoder_1_gs
  // Probe on priority_encoder_3_en_out
  Priority_Encoder #(.select(2), .disabled(0)) priority_encoder_2 (
    .in0(Rd), .in1(Rc), .in2(Rb), .in3(Ra), .out(priority_encoder_2_out), .gs(or_2_out[2]),
    .en_out(priority_encoder_2_en_out), .en_in(1'b1));
  Priority_Encoder #(.select(2), .disabled(0)) priority_encoder_3 (
    .in0(Rh), .in1(Rg), .in2(Rf), .in3(Re), .out(priority_encoder_3_out), .gs(priority_encoder_3_gs),
    .en_out(priority_encoder_3_en_out), .en_in(priority_encoder_2_en_out));
  // Priority_Encoder #(.select(2)) priority_encoder_4: pin names not known; wires that end beside it: in_3, in_6, priority_encoder_4_p3, in_8, priority_encoder_4_p5, priority_encoder_4_p6, priority_encoder_4_p7, priority_encoder_4_p8
  or or_1 (or_2_out[1], priority_encoder_2_out[1], priority_encoder_3_out[1]);
  or or_2 (or_2_out[0], priority_encoder_2_out[0], priority_encoder_3_out[0]);
  or or_3 (or_3_out, or_2_out[2], priority_encoder_3_gs);
  // Probe on priority_encoder_4_p3
  // Probe on priority_encoder_4_p5
  // Probe on priority_encoder_4_p6
  // Probe on priority_encoder_4_p7
  // Probe on priority_encoder_4_p8
  Decoder #(.select(2), .enable("false")) decoder_1 (
    .out0(decoder_1_out0), .out1(decoder_1_out1), .out2(decoder_1_out2), .out3(decoder_1_out3), .sel(in_14));
  // Probe on or_2_out
  Decoder #(.select(3)) decoder_2 (
    .out0(decoder_2_out0), .out1(decoder_2_out1), .out2(decoder_2_out2), .out3(decoder_2_out3),
    .out4(decoder_2_out4), .out5(decoder_2_out5), .out6(decoder_2_out6), .out7(decoder_2_out7),
    .sel(or_2_out), .en(or_3_out));
  buf buffer_1 (buffer_1_out, a);
  buf buffer_2 (buffer_1_out, b);
  // Probe on decoder_1_out0
  // Probe on decoder_1_out1
  // Probe on decoder_1_out2
  // Probe on decoder_1_out3
  Priority_Encoder priority_encoder_5 ();  // open: in0, in1, in2, in3, in4, in5, in6, in7, out, en_in, gs, en_out
  buf buffer_3 (buffer_1_out, c);
  buf buffer_4 (buffer_1_out, d);
  buf buffer_5 (buffer_1_out, e);
  buf buffer_6 (buffer_1_out, f);
  buf buffer_7 (buffer_1_out, g);
  buf buffer_8 (buffer_1_out, h);
  // Probe on buffer_1_out
  buf buffer_9 (buffer_9_out, i0);
  buf buffer_10 (i0_4, i0_5);

  assign i0_3 = i0;
  assign i0_7 = i0_6;

  // Notes on the sheet:
  //   Codificador de prioridade
  //   Codificador de prioridade
endmodule

module \Questão_7  (
  input  a,
  input  b
);

  wire decoder_1_out0, decoder_1_out1, priority_encoder_1_en_out, priority_encoder_1_gs;
  wire [1:0] priority_encoder_1_out;

  // Probe on priority_encoder_1_en_out
  Priority_Encoder #(.select(2), .disabled(0)) priority_encoder_1 (
    .in0(b), .in1(a), .in2(1'b0), .in3(1'b0), .out(priority_encoder_1_out), .gs(priority_encoder_1_gs),
    .en_out(priority_encoder_1_en_out), .en_in(1'b1));
  Decoder #(.select(2)) decoder_1 (
    .out0(decoder_1_out0), .out1(decoder_1_out1), .sel(priority_encoder_1_out), .en(priority_encoder_1_gs));  // open: out2, out3
  // Probe on decoder_1_out1
  // Probe on decoder_1_out0
endmodule

module somadores_de_4_bits (
  input  borrow_in,
  input  borrow_in_2,
  input  carry_in,
  input  carry_in_2,
  input  x1,
  input  [1:0] x1_2,
  input  x1_3,
  input  [1:0] x1_4,
  input  x2,
  input  [1:0] x2_2,
  input  x2_3,
  input  [1:0] x2_4,
  input  carry_in_3,
  input  carry_in_4,
  input  carry_in_5,
  input  A1,
  input  B1,
  input  A1_2,
  input  A2,
  input  A1_3,
  input  B1_2,
  input  B2,
  input  A2_2,
  input  A2_3,
  input  B2_2,
  input  B1_3,
  input  B2_3,
  input  A3,
  input  B3,
  input  A4,
  input  B4,
  input  borrow_in_3,
  input  carry_in_6,
  input  [2:0] x1_5,
  input  A1_4,
  input  B1_4,
  input  [2:0] x2_5,
  input  carry_in_7,
  input  A2_4,
  input  B2_4,
  input  A1_5,
  input  B1_5,
  input  carry_in_8,
  input  A3_2,
  input  B3_2,
  input  A2_5,
  input  A2_6,
  input  B2_5,
  input  B2_6,
  input  A3_3,
  input  B3_3,
  input  A2_7,
  input  B2_7,
  input  A4_2,
  input  B4_2,
  input  A2_8,
  input  carry_in_9,
  input  B2_8,
  input  [3:0] x1_6,
  input  A5,
  input  B5,
  input  [3:0] x2_6,
  input  A6,
  input  B6,
  input  A7,
  input  B7,
  input  A8,
  input  B8
);

  wire adder_1_cout, adder_1_out, adder_2_cout, adder_3_cout, adder_3_out, adder_4_cout, adder_4_out,
       adder_5_cout, adder_5_out, adder_6_cout, adder_6_out, adder_7_cout, adder_7_out, adder_8_cout,
       adder_9_cout, adder_9_out, adder_10_cout, adder_10_out, adder_11_cout, adder_11_out, adder_12_cout,
       adder_12_out, adder_13_cout, adder_13_out, adder_14_cout, adder_14_out, adder_15_cout, adder_15_out,
       adder_16_cout, adder_16_out, adder_17_cout, adder_17_out, adder_18_cout, adder_18_out, adder_19_cout,
       adder_19_out, adder_20_cout, adder_20_out, subtractor_1_bout, subtractor_1_out, subtractor_2_bout,
       subtractor_3_bout, subtractor_4_bout, subtractor_4_out, subtractor_5_bout, subtractor_5_out,
       subtractor_6_bout, subtractor_6_out, subtractor_7_bout, subtractor_7_out, subtractor_8_bout,
       subtractor_8_out;
  wire [1:0] adder_8_out, subtractor_2_out;
  wire [2:0] subtractor_3_out;
  wire [3:0] adder_2_out;

  // Probe on adder_1_out
  Adder #(.width(1)) adder_1 (.a(x1_3), .b(x2_3), .out(adder_1_out), .cin(carry_in), .cout(adder_1_cout));
  // Probe on adder_1_cout
  Adder #(.width(4)) adder_2 (.a(x1_6), .b(x2_6), .out(adder_2_out), .cin(carry_in_9), .cout(adder_2_cout));
  // Probe on adder_2_out
  // Probe on adder_2_cout
  Adder #(.width(1)) adder_3 (.a(A1_2), .b(B1_2), .out(adder_3_out), .cin(carry_in_4), .cout(adder_3_cout));
  // Probe on adder_3_out
  Adder #(.width(1)) adder_4 (.a(A2_2), .b(B2_3), .out(adder_4_out), .cin(adder_3_cout), .cout(adder_4_cout));
  // Probe on adder_4_cout
  // Probe on adder_4_out
  Adder #(.width(1)) adder_5 (.a(A1_4), .b(B1_4), .out(adder_5_out), .cin(carry_in_6), .cout(adder_5_cout));
  // Probe on adder_5_out
  Adder #(.width(1)) adder_6 (.a(A2_4), .b(B2_4), .out(adder_6_out), .cin(adder_5_cout), .cout(adder_6_cout));
  // Probe on adder_6_out
  Adder #(.width(1)) adder_7 (.a(A3_2), .b(B3_2), .out(adder_7_out), .cin(adder_6_cout), .cout(adder_7_cout));
  // Probe on adder_7_out
  // Probe on adder_7_cout
  Adder #(.width(2)) adder_8 (.a(x1_4), .b(x2_4), .out(adder_8_out), .cin(carry_in_2), .cout(adder_8_cout));
  // Probe on adder_8_out
  // Probe on adder_8_cout
  Subtractor #(.width(1)) subtractor_1 (
    .a(x1), .b(x2), .out(subtractor_1_out), .bin(borrow_in), .bout(subtractor_1_bout));
  // Probe on subtractor_1_out
  // Probe on subtractor_1_bout
  // Probe on adder_9_out
  Adder #(.width(1)) adder_9 (.a(A1), .b(B1), .out(adder_9_out), .cin(carry_in_3), .cout(adder_9_cout));
  Adder #(.width(1)) adder_10 (.a(A2_3), .b(B2_2), .out(adder_10_out), .cin(adder_9_cout), .cout(adder_10_cout));
  // Probe on adder_10_out
  Adder #(.width(1)) adder_11 (.a(A3), .b(B3), .out(adder_11_out), .cin(adder_10_cout), .cout(adder_11_cout));
  // Probe on adder_11_out
  // Probe on adder_12_out
  Adder #(.width(1)) adder_12 (.a(A4), .b(B4), .out(adder_12_out), .cin(adder_11_cout), .cout(adder_12_cout));
  // Probe on adder_12_cout
  Adder #(.width(1)) adder_13 (.a(A1_5), .b(B1_5), .out(adder_13_out), .cin(carry_in_7), .cout(adder_13_cout));
  // Probe on adder_13_out
  Adder #(.width(1)) adder_14 (.a(A2_6), .b(B2_5), .out(adder_14_out), .cin(adder_13_cout), .cout(adder_14_cout));
  // Probe on adder_14_out
  Adder #(.width(1)) adder_15 (.a(A3_3), .b(B3_3), .out(adder_15_out), .cin(adder_14_cout), .cout(adder_15_cout));
  // Probe on adder_15_out
  // Probe on adder_16_out
  Adder #(.width(1)) adder_16 (.a(A4_2), .b(B4_2), .out(adder_16_out), .cin(adder_15_cout), .cout(adder_16_cout));
  // Probe on adder_17_out
  Adder #(.width(1)) adder_17 (.a(A5), .b(B5), .out(adder_17_out), .cin(adder_16_cout), .cout(adder_17_cout));
  // Probe on adder_18_out
  Adder #(.width(1)) adder_18 (.a(A6), .b(B6), .out(adder_18_out), .cin(adder_17_cout), .cout(adder_18_cout));
  // Probe on adder_19_out
  Adder #(.width(1)) adder_19 (.a(A7), .b(B7), .out(adder_19_out), .cin(adder_18_cout), .cout(adder_19_cout));
  // Probe on adder_20_out
  Adder #(.width(1)) adder_20 (.a(A8), .b(B8), .out(adder_20_out), .cin(adder_19_cout), .cout(adder_20_cout));
  // Probe on adder_20_cout
  // Probe on subtractor_2_out
  Subtractor #(.width(2)) subtractor_2 (
    .a(x1_2), .b(x2_2), .out(subtractor_2_out), .bin(borrow_in_2), .bout(subtractor_2_bout));
  // Probe on subtractor_2_bout
  Subtractor #(.width(3)) subtractor_3 (
    .a(x1_5), .b(x2_5), .out(subtractor_3_out), .bin(borrow_in_3), .bout(subtractor_3_bout));
  // Probe on subtractor_3_out
  // Probe on subtractor_3_bout
  Subtractor #(.width(1)) subtractor_4 (
    .a(A2), .b(B2), .out(subtractor_4_out), .bin(carry_in_5), .bout(subtractor_4_bout));
  // Probe on subtractor_4_out
  // Probe on subtractor_5_out
  Subtractor #(.width(1)) subtractor_5 (
    .a(A1_3), .b(B1_3), .out(subtractor_5_out), .bin(subtractor_4_bout), .bout(subtractor_5_bout));
  // Probe on subtractor_5_bout
  // Probe on subtractor_6_out
  Subtractor #(.width(1)) subtractor_6 (
    .a(A2_5), .b(B2_6), .out(subtractor_6_out), .bin(carry_in_8), .bout(subtractor_6_bout));
  Subtractor #(.width(1)) subtractor_7 (
    .a(A2_7), .b(B2_7), .out(subtractor_7_out), .bin(subtractor_6_bout), .bout(subtractor_7_bout));
  // Probe on subtractor_7_out
  // Probe on subtractor_8_out
  Subtractor #(.width(1)) subtractor_8 (
    .a(A2_8), .b(B2_8), .out(subtractor_8_out), .bin(subtractor_7_bout), .bout(subtractor_8_bout));
  // Probe on subtractor_8_bout

  // Notes on the sheet:
  //   Somador de 1 bit
  //   +
  //   12
  //   Somador de 2 bits
  //   Somador de 2  bits
  //   Somador de 3  bits
  //   Somador de 2  bits
  //   12
  //   Somador de 4  bits
  //   Somador de 8 bits
  //   Subtrador de 1 bit
  //   Subtrador de 2  bits
  //   Subtrador de 2 bits
  //   Subtrador de 3  bits
  //   Subtrador de 3 bits
endmodule

module \Prova_questão_3  (
  input  a,
  input  b,
  input  cin,
  input  [2:0] A_2,
  input  [2:0] B_2,
  input  Cin_2,
  input  [5:0] A_3,
  input  [5:0] B_3,
  input  [2:0] Cin_3,
  input  [2:0] A_4,
  input  [2:0] B_4
);

  wire adder_1_cout, adder_2_cout, adder_3_cout, adder_4_cout, adder_5_cout, and_1_out, and_2_out, and_3_out,
       or_1_out, xor_1_out, xor_2_out;
  wire [2:0] adder_1_out, adder_3_out, multiplier_1_cout, multiplier_1_out;
  wire [5:3] adder_2_out;

  // Probe on or_1_out
  // Probe on xor_1_out
  and and_1 (and_1_out, a, b);
  or or_1 (or_1_out, and_1_out, and_2_out, and_3_out);
  and and_2 (and_2_out, a, cin);
  and and_3 (and_3_out, b, cin);
  xor xor_1 (xor_1_out, xor_2_out, cin);
  // Probe on adder_1_cout
  xor xor_2 (xor_2_out, a, b);
  Adder #(.width(3)) adder_1 (.a(A_3[2:0]), .b(B_3[2:0]), .out(adder_1_out), .cin(adder_2_cout), .cout(adder_1_cout));
  // Probe on {adder_2_out, adder_1_out}
  Adder #(.width(3)) adder_2 (.a(A_3[5:3]), .b(B_3[5:3]), .out(adder_2_out), .cout(adder_2_cout));  // open: cin
  Adder #(.width(1)) adder_3 (.a(A_2[0]), .b(B_2[0]), .out(adder_3_out[0]), .cin(adder_4_cout), .cout(adder_3_cout));
  // Probe on adder_3_cout
  // Probe on multiplier_1_cout
  Adder #(.width(1)) adder_4 (.a(A_2[1]), .b(B_2[1]), .out(adder_3_out[1]), .cin(adder_5_cout), .cout(adder_4_cout));
  // Probe on adder_3_out
  // Probe on multiplier_1_out
  Multiplier #(.width(3)) multiplier_1 (
    .a(A_4), .b(B_4), .out(multiplier_1_out), .cin(Cin_3), .cout(multiplier_1_cout));
  Adder #(.width(1)) adder_5 (.a(A_2[2]), .b(B_2[2]), .out(adder_3_out[2]), .cin(Cin_2), .cout(adder_5_cout));

  // Notes on the sheet:
  //   Somador de palavras de 6 bits incorreto da prova
  //   Multplicador de palavras de 3 bits 
  //   Somador de palavras de 3 bits incorreto da prova
endmodule

module \Prova_3_Questão_4  (
  input  [2:0] A,
  input  [2:0] A_2,
  input  [2:0] B,
  input  [2:0] B_2,
  input  [2:0] Cin,
  input  [2:0] A_3,
  input  [2:0] B_3,
  input  [5:0] A_4,
  input  [5:0] A_5,
  input  [5:0] Cin_2,
  input  [5:0] A_6,
  input  [5:0] B_4
);

  wire adder_2_cout, adder_2_out, adder_3_cout, adder_4_cout, adder_6_cout, adder_7_cout, adder_7_out,
       adder_8_cout, adder_9_cout, adder_10_cout, adder_11_cout, adder_13_cout, adder_13_out, adder_14_cout,
       adder_15_cout, adder_15_out, adder_16_cout, adder_17_cout, and_1_out, and_2_out, and_3_out, and_4_out,
       and_5_out, and_6_out, and_7_out, and_8_out, and_10_out, and_11_out, and_12_out, and_13_out,
       and_14_out, and_15_out, and_16_out, and_17_out;
  wire [0:0] adder_5_cout;
  wire [2:0] adder_3_out, adder_4_out, adder_5_out, adder_6_out, adder_9_out, adder_14_out, and_9_out,
       and_18_out, multiplier_1_cout, multiplier_1_out, multiplier_2_cout, multiplier_2_out,
       multiplier_3_cout, multiplier_3_out, multiplier_4_cout, multiplier_5_cout, multiplier_5_out;
  wire [5:0] multiplier_4_out, multiplier_6_cout, multiplier_6_out;

  and and_1 (and_1_out, A[2], B[2]);
  Adder #(.width(1)) adder_1 (
    .a(and_1_out), .b(adder_2_cout), .out(adder_3_out[1]), .cin(adder_3_cout), .cout(adder_3_out[2]));
  and and_2 (and_2_out, A[2], B[1]);
  and and_3 (and_3_out, A[1], B[2]);
  Adder #(.width(1)) adder_2 (.a(and_2_out), .b(and_3_out), .out(adder_2_out), .cin(adder_7_cout), .cout(adder_2_cout));
  Adder #(.width(1)) adder_3 (.a(1'b0), .b(adder_2_out), .out(adder_3_out[0]), .cin(adder_8_cout), .cout(adder_3_cout));
  Adder #(.width(3)) adder_4 (
    .a(multiplier_1_cout), .b({2'b00, adder_5_cout[0]}), .out(adder_4_out), .cin(adder_6_cout),
    .cout(adder_4_cout));
  and and_4 (and_4_out, A[0], B[2]);
  Multiplier #(.width(3)) multiplier_1 (
    .a(A_4[5:3]), .b(A_5[5:3]), .out(multiplier_1_out), .cout(multiplier_1_cout));  // open: cin
  Adder #(.width(3)) adder_5 (
    .a(multiplier_2_cout), .b(multiplier_3_cout), .out(adder_5_out), .cin(adder_9_cout),
    .cout(adder_5_cout[0]));
  Adder #(.width(3)) adder_6 (
    .a(multiplier_1_out), .b(adder_5_out), .out(adder_6_out), .cin(adder_10_cout), .cout(adder_6_cout));
  // Probe on {adder_4_out, adder_6_out}
  and and_5 (and_5_out, A[2], B[0]);
  and and_6 (and_6_out, A[1], B[1]);
  Adder #(.width(1)) adder_7 (
    .a(and_5_out), .b(and_6_out), .out(adder_7_out), .cin(adder_11_cout), .cout(adder_7_cout));
  Adder #(.width(1)) adder_8 (.a(and_4_out), .b(adder_7_out), .out(and_9_out[2]), .cin(1'b0), .cout(adder_8_cout));
  // Probe on adder_3_out
  Multiplier #(.width(3)) multiplier_2 (
    .a(A_4[2:0]), .b(A_5[5:3]), .out(multiplier_2_out), .cout(multiplier_2_cout));  // open: cin
  and and_7 (and_7_out, A[1], B[0]);
  // Probe on and_9_out
  Multiplier #(.width(3)) multiplier_3 (
    .a(A_4[5:3]), .b(A_5[2:0]), .out(multiplier_3_out), .cout(multiplier_3_cout));  // open: cin
  Adder #(.width(3)) adder_9 (
    .a(multiplier_3_out), .b(multiplier_4_cout), .out(adder_9_out), .cin(1'b0), .cout(adder_9_cout));
  Adder #(.width(3)) adder_10 (
    .a(multiplier_2_out), .b(adder_9_out), .out(multiplier_4_out[5:3]), .cin(1'b0), .cout(adder_10_cout));
  // Probe on multiplier_4_out
  and and_8 (and_8_out, A[0], B[1]);
  Adder #(.width(1)) adder_11 (.a(and_7_out), .b(and_8_out), .out(and_9_out[1]), .cin(1'b0), .cout(adder_11_cout));
  Multiplier #(.width(3)) multiplier_4 (
    .a(A_4[2:0]), .b(A_5[2:0]), .out(multiplier_4_out[2:0]), .cout(multiplier_4_cout));  // open: cin
  and and_9 (and_9_out[0], A[0], B[0]);
  and and_10 (and_10_out, A[2], B[2]);
  Adder #(.width(1)) adder_12 (
    .a(and_10_out), .b(adder_13_cout), .out(adder_14_out[1]), .cin(adder_14_cout), .cout(adder_14_out[2]));
  // Probe on multiplier_5_out
  Multiplier #(.width(3)) multiplier_5 (.a(A_3), .b(B_3), .out(multiplier_5_out), .cin(Cin), .cout(multiplier_5_cout));
  // Probe on multiplier_5_cout
  Multiplier #(.width(6)) multiplier_6 (
    .a(A_6), .b(B_4), .out(multiplier_6_out), .cin(Cin_2), .cout(multiplier_6_cout));
  // Probe on multiplier_6_cout
  and and_11 (and_11_out, A[1], B[2]);
  and and_12 (and_12_out, A[2], B[1]);
  Adder #(.width(1)) adder_13 (
    .a(and_12_out), .b(and_11_out), .out(adder_13_out), .cin(adder_15_cout), .cout(adder_13_cout));
  // Probe on multiplier_6_out
  and and_13 (and_13_out, A[0], B[2]);
  Adder #(.width(1)) adder_14 (
    .a(1'b0), .b(adder_13_out), .out(adder_14_out[0]), .cin(adder_16_cout), .cout(adder_14_cout));
  and and_14 (and_14_out, A[2], B[0]);
  and and_15 (and_15_out, A[1], B[1]);
  Adder #(.width(1)) adder_15 (.a(and_14_out), .b(and_15_out), .out(adder_15_out), .cin(1'b0), .cout(adder_15_cout));
  Adder #(.width(1)) adder_16 (
    .a(and_13_out), .b(adder_15_out), .out(and_18_out[2]), .cin(adder_17_cout), .cout(adder_16_cout));
  // Probe on adder_14_out
  and and_16 (and_16_out, A[1], B[0]);
  // Probe on and_18_out
  and and_17 (and_17_out, A[0], B[1]);
  Adder #(.width(1)) adder_17 (.a(and_16_out), .b(and_17_out), .out(and_18_out[1]), .cin(1'b0), .cout(adder_17_cout));
  and and_18 (and_18_out[0], A[0], B[0]);

  // Notes on the sheet:
  //   Multiplicador de 3 bits figura 4.5
  //   Multplicador de palavras de 3 bits 
  //   Multplicador de palavras de 6 bits 
  //   Multiplicador de 3 bits figura 4.6
endmodule

module \Prova_3_questão_5  (
  input  [3:0] A,
  input  [3:0] B,
  input  Cin,
  input  [2:0] S
);

  wire adder_1_cout, and_2_out;
  wire [3:0] adder_1_out, multiplexer_1_out, multiplexer_2_out, multiplexer_3_out, multiplexer_4_out,
       not_1_out, not_2_out, not_3_out, or_1_out;

  assign not_1_out = ~A;  // NOT_Gate not_1, 4 bits wide
  assign or_1_out = A | B;  // OR_Gate or_1, 4 bits wide
  // AND_Gate and_1 has open pins: in0=A, in1=B, out=open
  assign not_2_out = ~A;  // NOT_Gate not_2, 4 bits wide
  assign not_3_out = ~B;  // NOT_Gate not_3, 4 bits wide
  Multiplexer #(.select(2), .width(4)) multiplexer_1 (
    .in0(not_1_out), .in1(B), .in2(or_1_out), .out(multiplexer_1_out), .sel(S[1:0]));  // open: in3, en
  Multiplexer #(.select(2), .width(4)) multiplexer_2 (
    .in0(A), .in1(A), .in2(not_2_out), .in3(A), .out(multiplexer_2_out), .sel(S[1:0]));  // open: en
  Multiplexer #(.select(2), .width(4)) multiplexer_3 (
    .in0(B), .in1(not_3_out), .in2(B), .in3(4'b0000), .out(multiplexer_3_out), .sel(S[1:0]));  // open: en
  Multiplexer #(.width(4)) multiplexer_4 (
    .in0(multiplexer_1_out), .in1(adder_1_out), .out(multiplexer_4_out), .sel(S[2]));  // open: en
  Adder #(.width(4)) adder_1 (
    .a(multiplexer_2_out), .b(multiplexer_3_out), .out(adder_1_out), .cin(Cin), .cout(adder_1_cout));
  // Probe on multiplexer_4_out
  // Probe on and_2_out
  and and_2 (and_2_out, adder_1_cout, S[2]);
endmodule

module Prova4_1 (
  input  s,
  input  c,
  input  in_3
);

  wire and_1_out, and_2_out, nor_1_out, nor_2_out;

  and and_1 (and_1_out, s, c);
  and and_2 (and_2_out, c, in_3);
  nor nor_1 (nor_1_out, and_1_out, nor_2_out);
  nor nor_2 (nor_2_out, nor_1_out, and_2_out);
  // Probe on nor_2_out
endmodule
